// Logisim project FLIP-FLOP.circ as structural Verilog: 1 circuit, main circuit main
module main (
  input  RESET,
  input  RESET_2,
  input  SET,
  input  SET_2,
  input  in_5,
  input  in_6,
  input  in_7,
  input  S,
  input  D,
  input  R,
  input  J,
  input  J_2,
  input  K,
  input  K_2,
  output Q,
  output Q_2,
  output Q_prime,
  output Q_prime_2,
  output Q_3,
  output Q_4,
  output Q_5,
  output Q_prime_3,
  output Q_prime_4,
  output Q_prime_5,
  output Q_6,
  output Q_7,
  output Q_prime_6,
  output Q_prime_7,
  output Q_8,
  output Q_9,
  output Q_prime_8,
  output Q_prime_9
);

  wire and_1_out, and_2_out, and_3_out, and_4_out, CLK_2_out, CLK_3_out, CLK_4_out, CLK_out, nand_1_out,
       nand_2_out, not_1_out, not_2_out, not_3_out, not_4_out;

  Clock CLK (.out(CLK_out));
  Clock CLK_2 (.out(CLK_2_out));
  not not_1 (not_1_out, in_7);
  nand nand_1 (nand_1_out, S, CLK_out);
  nand nand_2 (nand_2_out, CLK_out, R);
  and and_1 (and_1_out, Q_prime_9, J, CLK_2_out);
  and and_2 (and_2_out, CLK_2_out, K_2, Q_8);
  nand nand_3 (Q, RESET, Q_prime);
  nand nand_4 (Q_prime, Q, SET);
  nand nand_5 (Q_5, in_7, Q_prime_5);
  nand nand_6 (Q_prime_5, Q_5, not_1_out);
  nand nand_7 (Q_6, nand_1_out, Q_prime_6);
  nand nand_8 (Q_prime_6, Q_6, nand_2_out);
  nor nor_1 (Q_8, and_1_out, Q_prime_9);
  nor nor_2 (Q_prime_9, Q_8, and_2_out);
  not not_2 (not_2_out, in_5);
  nor nor_3 (Q_2, RESET_2, Q_prime_2);
  nor nor_4 (Q_prime_2, Q_2, SET_2);
  nor nor_5 (Q_3, in_5, Q_prime_3);
  nor nor_6 (Q_prime_3, Q_3, not_2_out);
  not not_3 (not_3_out, D);
  Clock CLK_3 (.out(CLK_3_out));
  Clock CLK_4 (.out(CLK_4_out));
  and and_3 (and_3_out, not_3_out, CLK_3_out);
  and and_4 (and_4_out, CLK_3_out, D);
  J_K_Flip_Flop j_k_ff_1 (.J(J_2), .clk(CLK_4_out), .K(K), .Q(Q_9), .Qn(Q_prime_8));  // open: preset, en, reset
  not not_4 (not_4_out, in_6);
  nor nor_7 (Q_4, not_4_out, Q_prime_4);
  nor nor_8 (Q_prime_4, Q_4, in_6);
  nor nor_9 (Q_7, and_3_out, Q_prime_7);
  nor nor_10 (Q_prime_7, Q_7, and_4_out);

  // Notes on the sheet:
  //   FLIP-FLOP SR (SET-RESET)
  //   Excluimos o caso proibitivo do FLIP-FLOP SR
  //   FLIP-FLOP D
  //   FLIP-FLOP JK
  //   LATCH
  //   Duas formas de operações: FF Síncrono vs FF Assíncrono
  //   FF Síncrono
  //   FLIP-FLOP SR (SET-RESET)
  //   Excluimos o caso proibitivo do FLIP-FLOP SR
  //   FLIP-FLOP D
  //   Com o not aqui, armazenamos a saída
  //   FF D Síncrono
  //    Q assumirá O valor de J. Caso esperical: Quando J e K forem 1, ligar e desligar o clock alterna o resultado
  //   Excluimos o caso proibitivo do FLIP-FLOP SR
  //   FLIP-FLOP D
endmodule
