// Logisim project Painel Numerico.circ as structural Verilog: 1 circuit, main circuit main
module main (
  input  X,
  input  Y,
  input  W,
  input  Z,
  input  X_2,
  input  Y_2,
  input  W_2,
  input  Z_2,
  input  X_3,
  input  Y_3,
  input  W_3,
  input  Z_3,
  input  X_4,
  input  Y_4,
  input  W_4,
  input  Z_4,
  input  X_5,
  input  Y_5,
  input  W_5,
  input  Z_5,
  input  X_6,
  input  Y_6,
  input  W_6,
  input  Z_6,
  input  X_7,
  input  Y_7,
  input  W_7,
  input  Z_7
);

  wire and_1_out, and_2_out, and_3_out, and_4_out, and_5_out, and_6_out, and_7_out, and_8_out, and_9_out,
       and_10_out, and_11_out, and_12_out, and_13_out, and_14_out, and_15_out, and_16_out, and_17_out,
       and_18_out, and_19_out, and_20_out, and_21_out, and_22_out, and_23_out, and_24_out, and_25_out,
       and_26_out, and_27_out, and_28_out, and_29_out, and_30_out, and_31_out, not_1_out, not_2_out,
       not_3_out, not_4_out, not_5_out, not_6_out, not_7_out, not_8_out, not_9_out, not_10_out, not_11_out,
       not_12_out, not_13_out, not_14_out, not_15_out, not_16_out, not_17_out, not_18_out, not_19_out,
       not_20_out, not_21_out, not_22_out, not_23_out, not_24_out, not_25_out, not_26_out, not_27_out,
       not_28_out, or_1_out, or_2_out, or_3_out, or_4_out, or_5_out, or_6_out, or_7_out;

  not not_1 (not_1_out, X);
  not not_2 (not_2_out, W);
  and and_1 (and_1_out, not_1_out, Y, not_2_out);
  not not_3 (not_3_out, Y);
  and and_2 (and_2_out, not_1_out, not_3_out, W);
  or or_1 (or_1_out, and_1_out, and_2_out, and_4_out, and_6_out);
  and and_3 (and_3_out, W_5, not_5_out, not_4_out);
  not not_4 (not_4_out, X_5);
  not not_5 (not_5_out, Z_5);
  not not_6 (not_6_out, Z);
  and and_4 (and_4_out, not_1_out, W, not_6_out);
  or or_2 (or_2_out, and_3_out, and_5_out, and_7_out);
  and and_5 (and_5_out, not_7_out, not_5_out);
  not not_7 (not_7_out, Y_5);
  not not_8 (not_8_out, X_2);
  and and_6 (and_6_out, X, not_3_out, not_2_out);
  and and_7 (and_7_out, not_7_out, not_9_out, not_5_out);
  not not_9 (not_9_out, W_5);
  not not_10 (not_10_out, Z_2);
  not not_11 (not_11_out, W_2);
  and and_8 (and_8_out, not_8_out, not_11_out, not_10_out);
  and and_9 (and_9_out, not_8_out, Y_2, not_11_out);
  not not_12 (not_12_out, X_6);
  not not_13 (not_13_out, Y_2);
  and and_10 (and_10_out, not_13_out, not_11_out, not_10_out);
  or or_3 (or_3_out, and_8_out, and_9_out, and_10_out, and_12_out, and_14_out);
  and and_11 (and_11_out, not_12_out, not_14_out, W_6);
  not not_14 (not_14_out, Y_6);
  and and_12 (and_12_out, X_2, not_13_out, not_11_out);
  and and_13 (and_13_out, not_12_out, W_6, not_15_out);
  not not_15 (not_15_out, Z_6);
  and and_14 (and_14_out, not_8_out, Y_2, W_2, not_10_out);
  _7_Segment_Display u_7_segment_display_1 (
    .g(or_1_out), .f(or_3_out), .a(or_5_out), .b(or_7_out), .e(or_2_out), .d(or_4_out), .c(or_6_out));  // open: dp
  or or_4 (or_4_out, and_11_out, and_13_out, and_15_out, and_17_out, and_19_out);
  and and_15 (and_15_out, X_6, not_14_out, not_16_out);
  not not_16 (not_16_out, W_6);
  not not_17 (not_17_out, X_3);
  and and_16 (and_16_out, not_17_out, W_3);
  and and_17 (and_17_out, not_14_out, not_16_out, not_15_out);
  and and_18 (and_18_out, not_17_out, Y_3, Z_3);
  and and_19 (and_19_out, not_12_out, Y_6, not_16_out, Z_6);
  not not_18 (not_18_out, Z_3);
  not not_19 (not_19_out, Y_3);
  and and_20 (and_20_out, not_19_out, not_18_out);
  or or_5 (or_5_out, and_16_out, and_18_out, and_20_out, and_21_out, and_23_out);
  not not_20 (not_20_out, X_7);
  not not_21 (not_21_out, W_3);
  and and_21 (and_21_out, X_3, not_19_out, not_21_out);
  and and_22 (and_22_out, not_20_out, not_22_out);
  not not_22 (not_22_out, W_7);
  and and_23 (and_23_out, not_19_out, not_21_out, not_18_out);
  or or_6 (or_6_out, and_22_out, and_25_out, and_24_out, and_27_out, and_29_out);
  and and_24 (and_24_out, not_20_out, Y_7);
  and and_25 (and_25_out, not_20_out, Z_7);
  not not_23 (not_23_out, X_4);
  not not_24 (not_24_out, Y_4);
  and and_26 (and_26_out, not_23_out, not_24_out);
  and and_27 (and_27_out, not_25_out, not_22_out, not_28_out);
  not not_25 (not_25_out, Y_7);
  not not_26 (not_26_out, W_4);
  not not_27 (not_27_out, Z_4);
  and and_28 (and_28_out, not_23_out, not_26_out, not_27_out);
  or or_7 (or_7_out, and_26_out, and_28_out, and_31_out, and_30_out);
  and and_29 (and_29_out, X_7, not_25_out, not_22_out);
  not not_28 (not_28_out, Z_7);
  and and_30 (and_30_out, X_4, not_24_out, not_26_out);
  and and_31 (and_31_out, not_23_out, W_4, Z_4);
endmodule
