// Logisim project Registradores.circ as structural Verilog: 1 circuit, main circuit main
module main (
  input  Entrada,
  input  Entrada_2,
  input  Entrada_3,
  input  MR,
  input  PL,
  input  in_6,
  input  in_7,
  input  in_8,
  input  in_9,
  output \Saída ,
  output out_11,
  output out_12,
  output out_13,
  output \Saída_Serial ,
  output out_15,
  output out_16,
  output out_17,
  output \Saída_Serial_2 
);

  wire and_1_out, and_2_out, and_3_out, and_4_out, CLK_2_out, CLK_3_out, CLK_out, d_ff_1_q, d_ff_3_q,
       d_ff_6_q, not_1_out, not_2_out;

  Clock CLK (.out(CLK_out));
  Clock CLK_2 (.out(CLK_2_out));
  Clock CLK_3 (.out(CLK_3_out));
  not not_1 (not_1_out, MR);
  D_Flip_Flop d_ff_1 (.clk(CLK_out), .D(Entrada), .Q(d_ff_1_q));  // open: Qn, preset, en, reset
  D_Flip_Flop d_ff_2 (.clk(CLK_2_out), .D(Entrada_2), .Q(out_11));  // open: Qn, preset, en, reset
  and and_1 (and_1_out, in_6, PL);
  not not_2 (not_2_out, PL);
  D_Flip_Flop d_ff_3 (.clk(CLK_out), .D(d_ff_1_q), .Q(d_ff_3_q));  // open: Qn, preset, en, reset
  D_Flip_Flop d_ff_4 (.clk(CLK_2_out), .D(out_11), .Q(out_12));  // open: Qn, preset, en, reset
  D_Flip_Flop d_ff_5 (
    .clk(CLK_3_out), .D(Entrada_3), .Q(out_15), .preset(and_1_out), .en(not_2_out), .reset(not_1_out));  // open: Qn
  D_Flip_Flop d_ff_6 (.clk(CLK_out), .D(d_ff_3_q), .Q(d_ff_6_q));  // open: Qn, preset, en, reset
  D_Flip_Flop d_ff_7 (.clk(CLK_2_out), .D(out_12), .Q(out_13));  // open: Qn, preset, en, reset
  D_Flip_Flop d_ff_8 (
    .clk(CLK_3_out), .D(out_15), .Q(out_16), .preset(and_2_out), .en(not_2_out), .reset(not_1_out));  // open: Qn
  and and_2 (and_2_out, in_7, PL);
  D_Flip_Flop d_ff_9 (.clk(CLK_out), .D(d_ff_6_q), .Q(\Saída ));  // open: Qn, preset, en, reset
  D_Flip_Flop d_ff_10 (.clk(CLK_2_out), .D(out_13), .Q(\Saída_Serial ));  // open: Qn, preset, en, reset
  D_Flip_Flop d_ff_11 (
    .clk(CLK_3_out), .D(out_16), .Q(out_17), .preset(and_3_out), .en(not_2_out), .reset(not_1_out));  // open: Qn
  and and_3 (and_3_out, in_8, PL);
  D_Flip_Flop d_ff_12 (
    .clk(CLK_3_out), .D(out_17), .Q(\Saída_Serial_2 ), .preset(and_4_out), .en(not_2_out), .reset(not_1_out));  // open: Qn
  and and_4 (and_4_out, in_9, PL);

  // Notes on the sheet:
  //   PL - habilita a entrada Serial/Paralelo
  //   PL = 0 --> Entrada Serial
  //   PL = 1 --> Entrada Paralela
  //   Registrador Série-Série (Todo registrador serial tem a caracteristica de registrador de deslocamento)
  //   Registrador Série-Paralelo (A saída é simultânea)
  //   Conversor Serial/Paralelo - SHIFT REGISTER
  //   Sempre use o reset, pois a entrada PL não altera o valor do FF caso seja 1, logo, o reset vai garantir que o FF esteja armazenando 0.
  //   MR (master/reset) - limpa o registrador
  //   MR = 0 --> desabilita e reseta o registrador (FF = 0)
  //   MR = 1 --> permite a entrada de dados no registrador
endmodule
