// Logisim project Soma de 3 números de 2 bits.circ as structural Verilog: 1 circuit, main circuit main
module main (
  input  in_1,
  input  A______________B,
  input  in_3,
  input  in_4,
  input  C,
  input  in_6,
  input  in_7,
  output out_8,
  output A___B,
  output out_10,
  output A___B___C,
  output out_12,
  output out_13,
  output out_14
);

  wire adder_1_cout, adder_3_cout, adder_4_cout, undriven, undriven_2;

  Adder #(.width(1)) adder_1 (.a(in_4), .b(A______________B), .out(out_8), .cin(undriven), .cout(adder_1_cout));
  Adder #(.width(1)) adder_2 (.a(in_3), .b(in_1), .out(out_10), .cin(adder_1_cout), .cout(A___B));
  Adder #(.width(1)) adder_3 (.a(in_6), .b(out_8), .out(out_14), .cin(undriven_2), .cout(adder_3_cout));
  Adder #(.width(1)) adder_4 (.a(C), .b(out_10), .out(out_13), .cin(adder_3_cout), .cout(adder_4_cout));
  Adder #(.width(1)) adder_5 (.a(A___B), .b(in_7), .out(out_12), .cin(adder_4_cout), .cout(A___B___C));

  // Notes on the sheet:
  //   "vai um"
  //   0
endmodule
