// Logisim project Somador.circ as structural Verilog: 1 circuit, main circuit main
module main (
  input  A,
  input  B,
  input  B_2,
  input  B_3,
  input  A_2,
  input  A_3,
  output out_7,
  output out_8,
  output Overflow,
  output out_10,
  output out_11
);

  wire adder_1_cout, and_2_out, and_3_out, not_1_out, not_2_out;

  not not_1 (not_1_out, A);
  not not_2 (not_2_out, B);
  and and_1 (out_7, B, A);
  and and_2 (and_2_out, not_1_out, B);
  and and_3 (and_3_out, A, not_2_out);
  Adder #(.width(1)) adder_1 (.a(A_3), .b(B_3), .out(out_11), .cout(adder_1_cout));  // open: cin
  Adder #(.width(1)) adder_2 (.a(A_2), .b(B_2), .out(out_10), .cin(adder_1_cout), .cout(Overflow));
  // AND_Gate and_4 is placed but not wired
  or or_1 (out_8, and_2_out, and_3_out);

  // Notes on the sheet:
  //   Meio-Somador
  //   Somador Completo
  //   Resultado
endmodule
